# Fritzing sketch Untitled Sketch 8 (saved by Fritzing 0.9.4)
circuit board: 8.46667cm x 5.64444cm

parts:
  M1 = DOIT Esp32 DevKit v1 (30 pins long, 11 pins width) [part_number=ESP32S-PIN30]
  Componente1 = InvenSense MPU6050
  M2 = INA219 DC Current Monitor Module [part_number=CJMCU]
  U3 = Mini-360 DC-DC Buck converter [package=THT]
  U4 = Mini-360 DC-DC Buck converter [package=THT]
  C1 = Electrolytic Capacitor [capacitance=100μF package="0807 [SMD, electrolytic]"]
  U5 = SWITCH_SPDT [package=kps-1290]
  J7 = Dagu DGServo 9g header (male) [package=THT]
  J8 = Dagu DGServo 9g header (male) [package=THT]
  J9 = Dagu DGServo 9g header (male) [package=THT]
  J10 = Dagu DGServo 9g header (male) [package=THT]
  J11 = Dagu DGServo 9g header (male) [package=THT]
  J12 = Dagu DGServo 9g header (male) [package=THT]
  U2 = Mini-360 DC-DC Buck converter [package=THT]
  VCC1 = Battery
  J13 = Dagu DGServo 9g header (male) [package=THT]
  J14 = Dagu DGServo 9g header (male) [package=THT]
  J15 = Dagu DGServo 9g header (male) [package=THT]
  J16 = Dagu DGServo 9g header (male) [package=THT]
  J17 = Dagu DGServo 9g header (male) [package=THT]
  J18 = Dagu DGServo 9g header (male) [package=THT]
  J23 = Dagu DGServo 9g header (male) [package=THT]  # not connected
  J19 = Dagu DGServo 9g header (male) [package=THT]
  J22 = Dagu DGServo 9g header (male) [package=THT]  # not connected

nets:
  VCC: M1.3V3, Componente1.VCC, M2.VCC
  GND: M1.GND, Componente1.GND, M2.GND, U3.OUT-, C1.-
  N1: M1.D15, J19.gnd
  N2: M1.D2, J15.gnd
  N3: M1.D4, J18.gnd
  N4: M1.D5, J17.gnd
  N5: M1.D18, J13.gnd
  N6: M1.D19, J10.gnd
  N7: M1.D21, J7.gnd
  N8: M1.D22, J8.gnd
  N9: M1.D23, J12.gnd
  N10: M1.D33, J9.gnd
  N11: M1.D25, J11.gnd
  N12: M1.D26, J16.gnd
  N13: M1.D27, J14.gnd
  N14: M1.VIN, U3.OUT+, C1.+
  N15: Componente1.SCL, M2.SCL
  N16: Componente1.SDA, M2.SDA
  N17: M2.Vin-, U3.IN+, U4.IN+, U2.IN+
  N18: M2.Vin+, U5.O
  N19: U3.IN-, U4.IN-, U2.IN-, VCC1.-
  VCC_2: U4.OUT+, J7.Vcc, J8.Vcc, J9.Vcc, J10.Vcc, J11.Vcc, J12.Vcc
  N20: U4.OUT-, J7.pulse, J8.pulse, J9.pulse, J10.pulse, J11.pulse, J12.pulse
  N21: U5.P, U5.S, VCC1.+

custom parts:
  DOIT Esp32 DevKit v1 (30 pins long, 11 pins width): The DOIT Esp32 DevKit v1 is one of the development board created by DOIT to evaluate the ESP-WROOM-32 module. It is based on the ESP32 microcontroller that boasts Wifi, Bluetooth, Ethernet and Low Power support all in a single chip. (vanepp) made breadboard work, adjusted pin numbering and labels and reduced size of schematic and cleaned up pcb. This chip is 30pins long (2 x15) and 11 pins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
  INA219 DC Current Monitor Module: INA219 DC Current Monitor Module Links: INA219 product information
  Mini-360 DC-DC Buck converter: Mini-360 DC-DC Buck converter. Tiny buck step down voltage converter, input voltage 4.75 to 23V output 1 to 17V adjustable. Available from ebay and the like.
